// Logisim project TallerLogica-Combinatorios.circ as structural Verilog: 9 circuits, main circuit verificador
module sumador_simple (
  input  A,
  input  B,
  output S,
  output Cout
);

  xor xor_1 (S, A, B);
  and and_1 (Cout, A, B);
endmodule

module sumador_completo (
  input  Cin,
  input  A,
  input  B,
  output S,
  output Cout
);

  wire sumador_simple_1_cout, sumador_simple_1_s, sumador_simple_2_cout;

  sumador_simple sumador_simple_1 (.A(A), .B(B), .S(sumador_simple_1_s), .Cout(sumador_simple_1_cout));
  sumador_simple sumador_simple_2 (.A(Cin), .B(sumador_simple_1_s), .S(S), .Cout(sumador_simple_2_cout));
  or or_1 (Cout, sumador_simple_2_cout, sumador_simple_1_cout);
endmodule

module sumador_4 (
  input  Cin,
  input  [3:0] A,
  input  [3:0] B,
  output [3:0] S,
  output Cout
);

  wire sumador_completo_1_cout, sumador_completo_2_cout, sumador_completo_3_cout;

  sumador_completo sumador_completo_1 (.Cin(Cin), .A(A[0]), .B(B[0]), .S(S[0]), .Cout(sumador_completo_1_cout));
  sumador_completo sumador_completo_2 (
    .Cin(sumador_completo_1_cout), .A(A[1]), .B(B[1]), .S(S[1]), .Cout(sumador_completo_2_cout));
  sumador_completo sumador_completo_3 (
    .Cin(sumador_completo_2_cout), .A(A[2]), .B(B[2]), .S(S[2]), .Cout(sumador_completo_3_cout));
  sumador_completo sumador_completo_4 (.Cin(sumador_completo_3_cout), .A(A[3]), .B(B[3]), .S(S[3]), .Cout(Cout));
  Hex_Digit_Display hex_digit_display_1 (.value(S));  // open: dp
endmodule

module comparador_cero (
  input  [3:0] A,
  output Z
);

  wire not_1_out, not_2_out, or_1_out, or_2_out;

  or or_1 (or_1_out, A[0], A[1]);
  not not_1 (not_1_out, or_1_out);
  or or_2 (or_2_out, A[2], A[3]);
  not not_2 (not_2_out, or_2_out);
  and and_1 (Z, not_1_out, not_2_out);
endmodule

module sumador_flags (
  input  Cin,
  input  [3:0] A,
  input  [3:0] B,
  output [3:0] S,
  output C,
  output Z,
  output N,
  output V
);

  wire not_1_out, xor_1_out, xor_2_out;

  xor xor_1 (xor_1_out, B[3], A[3]);
  not not_1 (not_1_out, xor_1_out);
  sumador_4 sumador_4_1 (.Cin(Cin), .A(A), .B(B), .S({N, S[2:0]}), .Cout(C));
  xor xor_2 (xor_2_out, B[3], N);
  Hex_Digit_Display hex_digit_display_1 (.value({N, S[2:0]}));  // open: dp
  and and_1 (V, xor_2_out, not_1_out);
  comparador_cero comparador_cero_1 (.A({N, S[2:0]}), .Z(Z));

  assign S[3] = N;
endmodule

module incrementador_4 (
  input  [3:0] A,
  output [3:0] S
);

  Hex_Digit_Display hex_digit_display_1 (.value(S));  // open: dp
  sumador_4 sumador_4_1 (.Cin(1'b0), .A(A), .B(4'b0001), .S(S));  // open: Cout
endmodule

module inversor_4 (
  input  [3:0] A,
  input  INV,
  output [3:0] S
);

  wire [3:0] incrementador_4_1_s, not_1_out;

  assign not_1_out = ~A;  // NOT_Gate not_1, 4 bits wide
  incrementador_4 incrementador_4_1 (.A(not_1_out), .S(incrementador_4_1_s));
  Multiplexer #(.width(4)) multiplexer_1 (.in0(A), .in1(incrementador_4_1_s), .out(S), .sel(INV));
  Hex_Digit_Display hex_digit_display_1 (.value(S));  // open: dp
endmodule

module ALU (
  input  [1:0] OP,
  input  [3:0] A,
  input  [3:0] B,
  output N,
  output Z,
  output V,
  output C,
  output [3:0] S
);

  wire and_5_out, and_6_out, comparador_cero_1_z, multiplexer_1_out, multiplexer_2_out, multiplexer_3_out,
       not_1_out, not_2_out, not_3_out, not_4_out, not_5_out, not_6_out, not_7_out, sumador_4_1_cout,
       xor_1_out, xor_2_out;
  wire [3:0] and_4_out, inversor_4_1_s, or_4_out, sumador_4_1_s;

  and and_1 (and_4_out[3], A[3], B[3]);
  not not_1 (not_1_out, OP[1]);
  and and_2 (and_4_out[2], A[2], B[2]);
  and and_3 (and_4_out[1], A[1], B[1]);
  Multiplexer multiplexer_1 (.in0(OP[0]), .in1(not_1_out), .out(multiplexer_1_out), .sel(OP[1]));
  and and_4 (and_4_out[0], A[0], B[0]);
  or or_1 (or_4_out[3], A[3], B[3]);
  or or_2 (or_4_out[2], A[2], B[2]);
  inversor_4 inversor_4_1 (.A(B), .INV(multiplexer_1_out), .S(inversor_4_1_s));
  or or_3 (or_4_out[1], A[1], B[1]);
  or or_4 (or_4_out[0], A[0], B[0]);
  comparador_cero comparador_cero_1 (.A(B), .Z(comparador_cero_1_z));
  not not_2 (not_2_out, B[3]);
  Multiplexer multiplexer_2 (.in0(B[3]), .in1(not_2_out), .out(multiplexer_2_out), .sel(multiplexer_1_out));
  sumador_4 sumador_4_1 (.A(A), .B(inversor_4_1_s), .S(sumador_4_1_s), .Cout(sumador_4_1_cout));  // open: Cin
  not not_3 (not_3_out, comparador_cero_1_z);
  Multiplexer multiplexer_3 (.in0(sumador_4_1_cout), .in1(not_4_out), .out(multiplexer_3_out), .sel(multiplexer_1_out));
  not not_4 (not_4_out, sumador_4_1_cout);
  xor xor_1 (xor_1_out, multiplexer_2_out, N);
  xor xor_2 (xor_2_out, multiplexer_2_out, A[3]);
  not not_5 (not_5_out, xor_2_out);
  and and_5 (and_5_out, multiplexer_3_out, not_3_out);
  and and_6 (and_6_out, xor_1_out, not_5_out);
  Multiplexer #(.select(2), .width(4)) multiplexer_4 (
    .in0(sumador_4_1_s), .in1(sumador_4_1_s), .in2(and_4_out), .in3(or_4_out), .out({N, S[2:0]}), .sel(OP));
  Hex_Digit_Display hex_digit_display_1 (.value({N, S[2:0]}));  // open: dp
  and and_7 (C, and_5_out, not_6_out);
  not not_6 (not_6_out, OP[1]);
  not not_7 (not_7_out, OP[1]);
  comparador_cero comparador_cero_2 (.A({N, S[2:0]}), .Z(Z));
  and and_8 (V, and_6_out, not_7_out);

  assign S[3] = N;
endmodule

module verificador (
  output [3:0] out_1,
  output [3:0] out_2,
  output [1:0] out_3,
  output halt,
  output N,
  output Z,
  output V,
  output C,
  output [3:0] res
);

  wire clock_1_out;

  Clock clock_1 (.out(clock_1_out));
  Counter #(.max('h3ff), .width(10)) counter_1 (
    .clk(clock_1_out), .carry(halt), .Q({out_3, out_2, out_1}));  // open: clr, load, up, count, D
  // ALU alu_1: pin names not known; wires that end beside it: out_1, out_2, out_3, N, Z, V, C, res
endmodule
